# Fritzing sketch Breadboard_view_sensor_rumah_kepiting (saved by Fritzing 0.9.3b)
breadboards: 1

parts:
  DS1 = DS18B20 1-Wire Temperature Sensor Probe
  J1 = Screw terminal - 3 pins [package=THT]
  U1 = ESP8266 NodeMCU LoLin base
  R1 = Resistor [tolerance=±5% resistance=4.7k package=THT]
  M1 = PH meter with sensor in breadboard [package=THT]

nets:
  N1: DS1.GND, J1.pin1, U1.GND1-0, U1.GND2-0, U1.GND8-4, M1.pin3
  N2: DS1.DQ, J1.pin2, U1.D4-0, U1.D4-2, R1.Pin_0
  N3: DS1.VDD, J1.pin3, U1.3V1-0, U1.3V4, R1.Pin_1
  N4: U1.A0, M1.pin1
  N5: U1.5V-1, M1.pin2

custom parts:
  Screw terminal - 3 pins: Screw terminal with 3 pins (size increased to match part)
  ESP8266 NodeMCU LoLin base: ESP8266 based NodeMCU Base
  PH meter with sensor in breadboard: DFrobot PH meter (SKU SEN0161)
